// Logisim project NPC.circ as structural Verilog: 1 circuit, main circuit main
// NPC
module main (
  input  CQ_PASSED,
  input  in_2,
  input  [31:0] INSTRUCTION,
  input  [23:0] CURRENT_PC,
  input  [23:0] JUMP_ADDRESS,
  input  jump,
  output [23:0] NEXT_PC
);

  wire clk, Jump_Cmd, prev_jump, register_1_q;
  wire [4:0] undriven;
  wire [23:0] and_1_out, bit_extender_1_out, bit_extender_2_out, multiplexer_1_out, undriven_3;
  wire [31:0] inst, shifter_1_out, undriven_2;

  not not_1 (prev_jump, register_1_q);
  Register #(.width(1)) register_1 (.D(Jump_Cmd), .Q(register_1_q), .clk(clk));  // open: en, clr
  Multiplexer #(.width(24), .enable("false")) multiplexer_1 (
    .in0(CURRENT_PC), .in1(JUMP_ADDRESS), .out(multiplexer_1_out), .sel(jump));
  assign bit_extender_1_out = {{23{1'b0}}, CQ_PASSED};  // Bit_Extender bit_extender_1
  assign and_1_out = bit_extender_1_out & multiplexer_1_out;  // AND_Gate and_1, 24 bits wide
  assign bit_extender_2_out = {{23{1'b0}}, 1'b1};  // Bit_Extender bit_extender_2
  Adder #(.width(24)) adder_1 (.a(bit_extender_2_out), .b(and_1_out), .out(NEXT_PC));  // open: cin, cout
  // NOT_Gate not_2 has open pins: in=Jump_Cmd, out=open
  Register #(.width(32)) Instruction_Register (.D(inst), .en(CQ_PASSED), .clk(in_2));  // open: Q, clr
  Comparator #(.width(32)) comparator_1 (.a(undriven_2), .b(shifter_1_out));  // open: gt, eq, lt
  Shifter #(.width(32), .shift("lr")) shifter_1 (.\dist (undriven), .out(shifter_1_out));  // open: in
  Register #(.width(24)) pc (.D(undriven_3), .en(CQ_PASSED), .clk(in_2));  // open: Q, clr

  // Other names for the same wires on the sheet: clock = in_2; cPC[23:0] = CURRENT_PC; cqpass = CQ_PASSED;
  //   j[23:0] = JUMP_ADDRESS; jcontrol = jump; nextPC[23:0] = NEXT_PC

  // Notes on the sheet:
  //   NPC MODULE
endmodule
