// Logisim project PIP.circ as structural Verilog: 1 circuit, main circuit main
// PIP
module main (
  input  CQ_PASSED,
  input  [31:0] INSTRUCTION_IN,
  input  [23:0] PC_IN,
  input  CLOCK,
  output [31:0] INSTRUCTION_OUT,
  output [23:0] PC_OUT
);

  wire and_1_out, jcontrol, not_1_out;
  wire [3:0] bit_extender_1_out;
  wire [31:0] shifter_1_out;

  and and_1 (and_1_out, CQ_PASSED, not_1_out);
  Multiplexer #(.width(32)) multiplexer_1 (
    .in0({32{1'b0}}), .in1(INSTRUCTION_IN), .out(INSTRUCTION_OUT), .sel(and_1_out));  // open: en
  Register #(.width(24)) register_1 (.D(PC_IN), .en(CQ_PASSED), .Q(PC_OUT), .clk(CLOCK));  // open: clr
  not not_1 (not_1_out, jcontrol);
  Shifter #(.width(32), .shift("lr")) shifter_1 (.in(INSTRUCTION_IN), .\dist (5'b11100), .out(shifter_1_out));
  Bit_Extender #(.in_width(32), .out_width(4)) bit_extender_1 (.in(shifter_1_out), .out(bit_extender_1_out));
  Comparator #(.width(4)) comparator_1 (.a(4'b1111), .b(bit_extender_1_out), .eq(jcontrol));  // open: gt, lt

  // Other names for the same wires on the sheet: clk = CLOCK; cqpass = CQ_PASSED; inst[31:0] = INSTRUCTION_IN

  // Notes on the sheet:
  //   PIPELINE MODULE
endmodule
