// Logisim project REG.circ as structural Verilog: 1 circuit, main circuit main
// REG
module main (
  input  CLOCK,
  input  [3:0] REG_1_READ,
  input  [3:0] REG_2_READ,
  input  [3:0] REG_3_WRITE,
  input  [31:0] REG_WRITE_VAL,
  input  REG_WRITE,
  output [31:0] R00,
  output [31:0] R01,
  output [31:0] R02,
  output [31:0] R03,
  output [31:0] R04,
  output [31:0] R05,
  output [31:0] R06,
  output [31:0] R07,
  output [31:0] REG_1_VAL,
  output [31:0] REG_2_VAL,
  output [31:0] REG_3_VAL,
  output [31:0] R08,
  output [31:0] R09,
  output [31:0] R10,
  output [31:0] R11,
  output [31:0] R12,
  output [31:0] R13,
  output [31:0] R14,
  output [31:0] R15
);

  wire and_1_out, clk01, clk02, clk03, clk04, clk05, clk06, clk07, clk08, clk09, clk10, clk11, clk12, clk13,
       clk14, clk15;
  wire [31:0] wR00, wR01, wR02, wR03, wR04, wR05, wR06, wR07, wR08, wR09, wR10, wR11, wR12, wR13, wR14, wR15;

  Demultiplexer #(.select(4), .width(32)) demultiplexer_1 (
    .out0(wR00), .out1(wR01), .out2(wR02), .out3(wR03), .out4(wR04), .out5(wR05), .out6(wR06), .out7(wR07),
    .out8(wR08), .out9(wR09), .out10(wR10), .out11(wR11), .out12(wR12), .out13(wR13), .out14(wR14),
    .out15(wR15), .in(REG_WRITE_VAL), .sel(REG_3_WRITE));  // open: en
  Multiplexer #(.select(4), .width(32)) multiplexer_1 (
    .in0(R00), .in1(R01), .in2(R02), .in3(R03), .in4(R04), .in5(R05), .in6(R06), .in7(R07), .in8(R08),
    .in9(R09), .in10(R10), .in11(R11), .in12(R12), .in13(R13), .in14(R14), .in15(R15), .out(REG_1_VAL),
    .sel(REG_1_READ));  // open: en
  and and_1 (and_1_out, CLOCK, REG_WRITE);
  Demultiplexer #(.select(4)) demultiplexer_2 (
    .out1(clk01), .out2(clk02), .out3(clk03), .out4(clk04), .out5(clk05), .out6(clk06), .out7(clk07),
    .out8(clk08), .out9(clk09), .out10(clk10), .out11(clk11), .out12(clk12), .out13(clk13), .out14(clk14),
    .out15(clk15), .in(and_1_out), .sel(REG_3_WRITE));  // open: out0, en
  Register #(.width(32)) u_R12 (.D(wR12), .Q(R12), .clk(clk12));  // open: en, clr
  Register #(.width(32)) u_R13 (.D(wR13), .Q(R13), .clk(clk13));  // open: en, clr
  Register #(.width(32)) u_R14 (.D(wR14), .Q(R14), .clk(clk14));  // open: en, clr
  Register #(.width(32)) u_R15 (.D(wR15), .Q(R15), .clk(clk15));  // open: en, clr
  Multiplexer #(.select(4), .width(32)) multiplexer_2 (
    .in0(R00), .in1(R01), .in2(R02), .in3(R03), .in4(R04), .in5(R05), .in6(R06), .in7(R07), .in8(R08),
    .in9(R09), .in10(R10), .in11(R11), .in12(R12), .in13(R13), .in14(R14), .in15(R15), .out(REG_2_VAL),
    .sel(REG_2_READ));  // open: en
  Register #(.width(32)) u_R00 (.Q(R00));  // open: D, en, clk, clr
  Register #(.width(32)) u_R01 (.D(wR01), .Q(R01), .clk(clk01));  // open: en, clr
  Register #(.width(32)) u_R02 (.D(wR02), .Q(R02), .clk(clk02));  // open: en, clr
  Register #(.width(32)) u_R03 (.D(wR03), .Q(R03), .clk(clk03));  // open: en, clr
  Register #(.width(32)) u_R04 (.D(wR04), .Q(R04), .clk(clk04));  // open: en, clr
  Register #(.width(32)) u_R05 (.D(wR05), .Q(R05), .clk(clk05));  // open: en, clr
  Register #(.width(32)) u_R06 (.D(wR06), .Q(R06), .clk(clk06));  // open: en, clr
  Register #(.width(32)) u_R07 (.D(wR07), .Q(R07), .clk(clk07));  // open: en, clr
  Register #(.width(32)) u_R08 (.D(wR08), .Q(R08), .clk(clk08));  // open: en, clr
  Register #(.width(32)) u_R09 (.D(wR09), .Q(R09), .clk(clk09));  // open: en, clr
  Register #(.width(32)) u_R10 (.D(wR10), .Q(R10), .clk(clk10));  // open: en, clr
  Register #(.width(32)) u_R11 (.D(wR11), .Q(R11), .clk(clk11));  // open: en, clr
  Multiplexer #(.select(4), .width(32)) multiplexer_3 (
    .in0(R00), .in1(R01), .in2(R02), .in3(R03), .in4(R04), .in5(R05), .in6(R06), .in7(R07), .in8(R08),
    .in9(R09), .in10(R10), .in11(R11), .in12(R12), .in13(R13), .in14(R14), .in15(R15), .out(REG_3_VAL),
    .sel(REG_3_WRITE));  // open: en

  // Other names for the same wires on the sheet: clk = CLOCK; IR00[31:0] = R00; IR01[31:0] = R01; IR02[31:0] = R02;
  //   IR03[31:0] = R03; IR04[31:0] = R04; IR05[31:0] = R05; IR06[31:0] = R06; IR07[31:0] = R07; IR08[31:0] = R08;
  //   IR09[31:0] = R09; IR10[31:0] = R10; IR11[31:0] = R11; IR12[31:0] = R12; IR13[31:0] = R13; IR14[31:0] = R14;
  //   IR15[31:0] = R15; reg1Read[3:0] = REG_1_READ; reg1Val[31:0] = REG_1_VAL; reg2Read[3:0] = REG_2_READ;
  //   reg2Val[31:0] = REG_2_VAL; reg3Val[31:0] = REG_3_VAL; reg3Write[3:0] = REG_3_WRITE; write = REG_WRITE

  // Notes on the sheet:
  //   REGISTER FILE MODULE
endmodule
